// Digital circuit Capstone_Display.dig as structural Verilog
module Capstone_Display (
  input  D,
  input  V,
  input  clk,
  output L,
  output M
);

  wire _1, _2, _3, A, A_t, and_1_out, and_2_out, and_3_out, and_4_out, and_5_out, and_7_out, B, C, or_1_out,
       or_2_out, or_3_out, xnor_1_out;

  D_FF u_A (.D(or_1_out), .C(clk), .Q(A), .nQ(A_t));
  D_FF u_B (.D(or_2_out), .C(clk), .Q(B), .nQ(L));
  D_FF u_C (.D(or_3_out), .C(clk), .Q(C), .nQ(M));
  or or_1 (or_1_out, and_1_out, and_2_out);
  and and_1 (and_1_out, A, B);
  and and_2 (and_2_out, A_t, L, C);
  or or_2 (or_2_out, and_3_out, V);
  and and_3 (and_3_out, A_t, C, D);
  and and_4 (and_4_out, A, B);
  or or_3 (or_3_out, and_4_out, and_5_out, D, V);
  and and_5 (and_5_out, A_t, L, C);
  LED led_1 (.in(_2));
  LED led_2 (.in(_2));
  LED led_3 (.in(_2));
  LED led_4 (.in(_2));
  LED led_5 (.in(_2));
  LED led_6 (.in(_2));
  LED led_7 (.in(_2));
  LED led_8 (.in(_2));
  LED led_9 (.in(_2));
  LED led_10 (.in(_2));
  LED led_11 (.in(_1));
  LED led_12 (.in(_1));
  LED led_13 (.in(_1));
  LED led_14 (.in(_1));
  LED led_15 (.in(_1));
  LED led_16 (.in(_1));
  LED led_17 (.in(1'b1));
  LED led_18 (.in(1'b1));
  LED led_19 (.in(_2));
  LED led_20 (.in(_2));
  LED led_21 (.in(_2));
  LED led_22 (.in(_2));
  LED led_23 (.in(C));
  LED led_24 (.in(C));
  LED led_25 (.in(_2));
  LED led_26 (.in(_2));
  LED led_27 (.in(_2));
  LED led_28 (.in(_2));
  LED led_29 (.in(_1));
  LED led_30 (.in(_1));
  LED led_31 (.in(_1));
  LED led_32 (.in(_1));
  LED led_33 (.in(_1));
  LED led_34 (.in(_1));
  LED led_35 (.in(1'b1));
  LED led_36 (.in(1'b1));
  LED led_37 (.in(_2));
  LED led_38 (.in(_2));
  LED led_39 (.in(_2));
  LED led_40 (.in(_2));
  LED led_41 (.in(C));
  LED led_42 (.in(C));
  LED led_43 (.in(_2));
  LED led_44 (.in(_2));
  LED led_45 (.in(_2));
  LED led_46 (.in(_2));
  LED led_47 (.in(_2));
  LED led_48 (.in(_2));
  LED led_49 (.in(_2));
  LED led_50 (.in(_2));
  LED led_51 (.in(_2));
  LED led_52 (.in(_2));
  LED led_53 (.in(1'b1));
  LED led_54 (.in(1'b1));
  LED led_55 (.in(_3));
  LED led_56 (.in(_3));
  LED led_57 (.in(_3));
  LED led_58 (.in(_3));
  LED led_59 (.in(C));
  LED led_60 (.in(C));
  LED led_61 (.in(_3));
  LED led_62 (.in(_3));
  LED led_63 (.in(_3));
  LED led_64 (.in(_3));
  LED led_65 (.in(_2));
  LED led_66 (.in(A));
  LED led_67 (.in(_2));
  LED led_68 (.in(A));
  LED led_69 (.in(_2));
  LED led_70 (.in(A));
  LED led_71 (.in(1'b1));
  LED led_72 (.in(1'b1));
  LED led_73 (.in(_3));
  LED led_74 (.in(_3));
  LED led_75 (.in(_3));
  LED led_76 (.in(_3));
  LED led_77 (.in(C));
  LED led_78 (.in(C));
  LED led_79 (.in(_3));
  LED led_80 (.in(_3));
  LED led_81 (.in(_3));
  LED led_82 (.in(_3));
  LED led_83 (.in(A));
  LED led_84 (.in(A));
  LED led_85 (.in(A));
  LED led_86 (.in(A));
  LED led_87 (.in(A));
  LED led_88 (.in(A));
  LED led_89 (.in(1'b1));
  LED led_90 (.in(1'b1));
  LED led_91 (.in(_3));
  LED led_92 (.in(_3));
  LED led_93 (.in(C));
  LED led_94 (.in(_3));
  LED led_95 (.in(_3));
  LED led_96 (.in(A));
  LED led_97 (.in(A));
  LED led_98 (.in(A));
  LED led_99 (.in(1'b1));
  xnor xnor_1 (xnor_1_out, B, A);
  and and_6 (_2, B, A_t);
  and and_7 (and_7_out, C, L);
  and and_8 (_1, xnor_1_out, C);
  or or_4 (_3, A, and_7_out);

  // Other names for the same wires on the sheet: B_t = L; C_t = M; X = _3
endmodule
