// Digital circuit Capstone_Regular.dig as structural Verilog
module Capstone_Regular (
  input  D,
  input  V,
  input  clk,
  output L,
  output M
);

  wire A, A_nq, and_1_out, and_2_out, and_3_out, and_4_out, and_5_out, B, C, or_1_out, or_2_out, or_3_out;

  D_FF u_A (.D(or_1_out), .C(clk), .Q(A), .nQ(A_nq));
  D_FF u_B (.D(or_2_out), .C(clk), .Q(B), .nQ(L));
  D_FF u_C (.D(or_3_out), .C(clk), .Q(C), .nQ(M));
  or or_1 (or_1_out, and_1_out, and_2_out);
  and and_1 (and_1_out, A, B);
  and and_2 (and_2_out, A_nq, L, C);
  or or_2 (or_2_out, and_3_out, V);
  and and_3 (and_3_out, A_nq, C, D);
  and and_4 (and_4_out, A, B);
  or or_3 (or_3_out, and_4_out, and_5_out, D, V);
  and and_5 (and_5_out, A_nq, L, C);
endmodule
